# Fritzing sketch moisture_sensor_v1 (saved by Fritzing 1.0.2b)
circuit board: 4.751cm x 12.3655cm
breadboards: 1

parts:
  R1 = Resistor [tolerance=±5% power=0.25W resistance=220 package=THT]
  LED1 = LED - 5mm [color="Red (633nm)" current=0.030A package="5 mm [THT]"]
  BAT1 = BC9VPC [package=bc9vpc]
  nano = Arduino Nano (Rev3.0)
  S1 = Pushbutton [package="[THT]"]  # not connected
  LED2 = LED - 5mm [color="Red (633nm)" current=0.030A package="5 mm [THT]"]
  LED3 = LED - 5mm [color="Red (633nm)" current=0.030A package="5 mm [THT]"]
  LED4 = LED - 5mm [color="Red (633nm)" current=0.030A package="5 mm [THT]"]
  LED5 = LED - 5mm [color="Red (633nm)" current=0.030A package="5 mm [THT]"]
  R2 = Resistor [tolerance=±5% power=0.25W resistance=220 package=THT]
  R3 = Resistor [tolerance=±5% power=0.25W resistance=220 package=THT]
  R4 = Resistor [tolerance=±5% power=0.25W resistance=220 package=THT]
  R5 = Resistor [tolerance=±5% power=0.25W resistance=220 package=THT]

nets:
  N1: R1.Pin_0, BAT1.V-, nano.GND, R2.Pin_1, R3.Pin_1, R4.Pin_1, R5.Pin_1
  N2: R1.Pin_1, LED1.cathode
  N3: LED1.anode, nano.D2
  N4: nano.D3, LED2.anode
  N5: nano.D4, LED3.anode
  N6: nano.D5, LED4.anode
  N7: nano.D6, LED5.anode
  N8: LED2.cathode, R2.Pin_0
  N9: LED3.cathode, R3.Pin_0
  N10: LED4.cathode, R4.Pin_0
  N11: LED5.cathode, R5.Pin_0
